// Logisim project cpu.circ as structural Verilog: 1 circuit, main circuit cpu
module cpu (
  input  clk,
  input  [31:0] INSTRUCTION,
  input  [31:0] READ_DATA,
  output [31:0] WRITE_ADDRESS,
  output [31:0] PROGRAM_COUNTER,
  output [31:0] ra,
  output [31:0] sp,
  output [31:0] t0,
  output [31:0] t1,
  output [31:0] t2,
  output [31:0] s0,
  output [31:0] s1,
  output [31:0] a0,
  output [31:0] tohost,
  output [3:0] WRITE_ENABLE,
  output [31:0] WRITE_DATA
);

  wire ASel, BrEq, BrLt, BrUn, BSel, CSRSel, CSRWen, MemRW, PCSel, RegWEn;
  wire [1:0] WBSel;
  wire [2:0] ImmSel;
  wire [3:0] ALUSel, mask, sb, sh;
  wire [31:0] bhwdata, bit_extender_1_out, bit_extender_2_out, bit_extender_3_out, bit_extender_4_out,
       bit_extender_5_out, bit_extender_6_out, bit_extender_7_out, bit_extender_8_out, bit_extender_9_out,
       csr_din, final_READ_DATA, imm, input_a, input_b, PC4, pc_in, read_reg1, read_reg2, shifter_1_out,
       shifter_2_out, shifter_3_out, shifter_4_out, shifter_5_out, Write_Data_t;

  Adder #(.width(32)) adder_1 (.a(PROGRAM_COUNTER), .b(32'h4), .out(PC4));  // open: cin, cout
  Register #(.width(32)) PC (.D(pc_in), .clk(clk), .Q(PROGRAM_COUNTER));  // open: en, clr
  Multiplexer #(.enable("false"), .width(32)) multiplexer_1 (.in0(PC4), .in1(WRITE_ADDRESS), .out(pc_in), .sel(PCSel));
  control_logic control_logic_1 (
    .CSRWen(CSRWen), .PCSel(PCSel), .RegWEn(RegWEn), .ImmSel(ImmSel), .BrUn(BrUn), .ASel(ASel), .BSel(BSel),
    .ALUSel(ALUSel), .MemRW(MemRW), .WBSel(WBSel), .CSRSel(CSRSel), .inst(INSTRUCTION), .BrEq(BrEq),
    .BrLt(BrLt));
  imm_gen imm_gen_1 (.inst(INSTRUCTION), .ImmSel(ImmSel), .imm(imm));
  regfile regfile_1 (
    .rs1(INSTRUCTION[19:15]), .rs2(INSTRUCTION[24:20]), .rd(INSTRUCTION[11:7]), .Write_Data(Write_Data_t),
    .RegWEn(RegWEn), .clk(clk), .ra(ra), .sp(sp), .t0(t0), .t1(t1), .t2(t2), .s0(s0), .s1(s1), .a0(a0),
    .Read_Data_1(read_reg1), .Read_Data_2(read_reg2));
  branch_comp branch_comp_1 (.rs1(read_reg1), .rs2(read_reg2), .BrUn(BrUn), .BrEq(BrEq), .BrLt(BrLt));
  Multiplexer #(.enable("false"), .width(32)) multiplexer_2 (.in0(read_reg2), .in1(imm), .out(input_b), .sel(BSel));
  Multiplexer #(.enable("false"), .width(32)) multiplexer_3 (
    .in0(PROGRAM_COUNTER), .in1(read_reg1), .out(input_a), .sel(ASel));
  Multiplexer #(.enable("false"), .select(3), .width(32)) multiplexer_4 (
    .in1(read_reg1), .in5(imm), .out(csr_din), .sel(INSTRUCTION[14:12]));  // open: in0, in2, in3, in4, in6, in7
  // csr csr_1: pin names not known; wires that end beside it: INSTRUCTION[31:20], csr_din, CSRWen, clk, tohost
  alu alu_1 (.Result(WRITE_ADDRESS), .A(input_a), .B(input_b), .ALUSel(ALUSel));
  Shifter #(.width(32)) shifter_1 (.in(bhwdata), .\dist (5'b10000), .out(shifter_1_out));
  Shifter #(.width(32)) shifter_2 (.in(bhwdata), .\dist (5'b01000), .out(shifter_2_out));
  Shifter #(.width(32)) shifter_3 (.in(bhwdata), .\dist (5'b11000), .out(shifter_3_out));
  assign bit_extender_1_out = {{24{1'b0}}, read_reg2[7:0]};  // Bit_Extender bit_extender_1
  assign bit_extender_2_out = {{16{1'b0}}, read_reg2[15:0]};  // Bit_Extender bit_extender_2
  Shifter #(.width(32)) shifter_4 (.in(bhwdata), .\dist (5'b01000), .out(shifter_4_out));
  Shifter #(.width(32)) shifter_5 (.in(bhwdata), .\dist (5'b10000), .out(shifter_5_out));
  Multiplexer #(.enable("false"), .select(3), .width(32)) multiplexer_5 (
    .in0(bit_extender_1_out), .in1(bit_extender_2_out), .in2(read_reg2), .out(bhwdata),
    .sel(INSTRUCTION[14:12]));  // open: in3, in4, in5, in6, in7
  Multiplexer #(.enable("false"), .select(4), .width(32)) multiplexer_6 (
    .in1(bhwdata), .in2(shifter_2_out), .in3(bhwdata), .in4(shifter_1_out), .in6(shifter_4_out),
    .in8(shifter_3_out), .in12(shifter_5_out), .in15(bhwdata), .out(WRITE_DATA), .sel(mask));  // open: in0, in5, in7, in9, in10, in11, in13, in14
  Multiplexer #(.enable("false"), .select(3), .width(4)) multiplexer_7 (
    .in0(sb), .in1(sh), .in2(4'b1111), .out(mask), .sel(INSTRUCTION[14:12]));  // open: in3, in4, in5, in6, in7
  Multiplexer #(.enable("false"), .select(2), .width(4)) multiplexer_8 (
    .in0(4'b0001), .in1(4'b0010), .in2(4'b0100), .in3(4'b1000), .out(sb), .sel(WRITE_ADDRESS[1:0]));
  Multiplexer #(.enable("false"), .select(2), .width(4)) multiplexer_9 (
    .in0(4'b0011), .in1(4'b0110), .in2(4'b1100), .out(sh), .sel(WRITE_ADDRESS[1:0]));  // open: in3
  Multiplexer #(.enable("false"), .width(4)) multiplexer_10 (
    .in0(4'b0000), .in1(mask), .out(WRITE_ENABLE), .sel(MemRW));
  assign bit_extender_3_out = {{24{READ_DATA[23]}}, READ_DATA[23:16]};  // Bit_Extender bit_extender_3
  assign bit_extender_4_out = {{24{READ_DATA[7]}}, READ_DATA[7:0]};  // Bit_Extender bit_extender_4
  assign bit_extender_5_out = {{24{READ_DATA[15]}}, READ_DATA[15:8]};  // Bit_Extender bit_extender_5
  assign bit_extender_6_out = {{16{READ_DATA[15]}}, READ_DATA[15:0]};  // Bit_Extender bit_extender_6
  assign bit_extender_7_out = {{16{READ_DATA[23]}}, READ_DATA[23:8]};  // Bit_Extender bit_extender_7
  assign bit_extender_8_out = {{24{READ_DATA[31]}}, READ_DATA[31:24]};  // Bit_Extender bit_extender_8
  assign bit_extender_9_out = {{16{READ_DATA[31]}}, READ_DATA[31:16]};  // Bit_Extender bit_extender_9
  Multiplexer #(.enable("false"), .select(4), .width(32)) multiplexer_11 (
    .in1(bit_extender_4_out), .in2(bit_extender_5_out), .in3(bit_extender_6_out), .in4(bit_extender_3_out),
    .in6(bit_extender_7_out), .in8(bit_extender_8_out), .in12(bit_extender_9_out), .in15(READ_DATA),
    .out(final_READ_DATA), .sel(mask));  // open: in0, in5, in7, in9, in10, in11, in13, in14
  Multiplexer #(.enable("false"), .select(2), .width(32)) multiplexer_12 (
    .in0(PC4), .in1(WRITE_ADDRESS), .in2(final_READ_DATA), .out(Write_Data_t), .sel(WBSel));  // open: in3

  // Other names for the same wires on the sheet: ALU_out[31:0] = WRITE_ADDRESS; last2bits[1:0] = WRITE_ADDRESS[1:0];
  //   csr_addr[11:0] = INSTRUCTION[31:20]; inst[31:0] = INSTRUCTION; rs2[4:0] = INSTRUCTION[24:20];
  //   funct3[2:0] = INSTRUCTION[14:12]; rd[4:0] = INSTRUCTION[11:7]; rs1[4:0] = INSTRUCTION[19:15];
  //   opcode[6:0] = INSTRUCTION[6:0]

  // Notes on the sheet:
  //   Output to IMEM
  //   IMEM (do **NOT** move this)
  //   Inputs from IMEM
  //   It is OK to move the PC, RegFile, ALU, MEM, Branch Comp, Imm Gen, and Control Logic to wherever is most convenient for you when constructing your CPU, and to delete this text
  //   Inputs/Outputs for testing. Do **NOT** move these.
  //   Outputs To DMEM
  //   DMEM (do **NOT** move this)
  //   Inputs From DMEM
endmodule
